# Fritzing sketch booster (saved by Fritzing 0.9.2b)
breadboards: 1

parts:
  L1 = Inductor [inductance=2.2mH package="400 mil [THT]"]
  R4 = Resistor [tolerance=±5% resistance=100 package=THT]
  R2 = Resistor [tolerance=±5% resistance=10k package=THT]
  R5 = Resistor [tolerance=±5% resistance=10k package=THT]
  Q3 = Basic FET N-Channel [part_number=IRF710 package="TO220 [THT]"]
  R3 = Resistor [tolerance=±5% resistance=100 package=THT]
  R6 = Resistor [tolerance=±5% resistance=100 package=THT]
  Q4 = Basic FET N-Channel [part_number=IRF710 package="TO220 [THT]"]
  Arduino_Uno = Arduino Uno (Rev3)
  L2 = Inductor [package="400 mil [THT]"]
  D1 = Rectifier Diode [part_number=1N4007 package="300 mil [THT]"]
  C1 = Electrolytic Capacitor [capacitance=47µF package="300 mil [THT, electrolytic]"]
  R1 = Resistor [tolerance=±5% resistance=100 package=THT]
  D2 = Rectifier Diode [part_number=1N4007 package="Melf DO-213 AB [SMD]"]
  Q1 = Basic FET N-Channel [part_number=IRLB8748PBF package="TO220 [THT]"]
  Q2 = Basic FET N-Channel [part_number=IRLB8748PBF package="TO220 [THT]"]
  VCC1 = Battery block 9V [part_number=7.4V]

nets:
  N1: L1.pin_0, Arduino_Uno.VIN, Q1.drain, Q2.drain, VCC1.+
  N2: L1.pin_1, Q3.drain, D1.anode
  N3: R4.Pin_0, Arduino_Uno.D9_PWM
  N4: R4.Pin_1, Q2.gate
  N5: R2.Pin_0, R5.Pin_0, Q3.source, Q4.source, Arduino_Uno.GND, C1.-, VCC1.-
  N6: R2.Pin_1, R3.Pin_0, Q1.source
  N7: R5.Pin_1, R6.Pin_0, Q2.source
  N8: Q3.gate, R3.Pin_1
  N9: R6.Pin_1, Q4.gate
  N10: Q4.drain, L2.pin_1, D2.anode
  N11: Arduino_Uno.D8, R1.Pin_0
  N12: L2.pin_0, D1.cathode, C1.+, D2.cathode
  N13: R1.Pin_1, Q1.gate

notes:
  4 kHz
  92%
  25 Hz
  50%
